// Logisim project ejemplo1_clase.circ as structural Verilog: 2 circuits, main circuit main
module main (
  input  A,
  input  B,
  input  C,
  output F
);

  circuito1 circuito1_1 (.A(A), .B(B), .C(C), .F(F));
endmodule

module circuito1 (
  input  A,
  input  B,
  input  C,
  output F
);

  wire and_1_out, and_2_out, and_3_out, or_1_out;

  and and_1 (and_1_out, A, B);
  or or_1 (or_1_out, B, C);
  and and_2 (and_2_out, A, or_1_out);
  and and_3 (and_3_out, or_1_out, B);
  or or_2 (F, and_1_out, and_2_out, and_3_out);
endmodule
