// Logisim project circuito_ejemplo3a.circ as structural Verilog: 1 circuit, main circuit main
module main (
  input  P,
  input  Q,
  output R
);

  wire not_1_out;

  // Probe on Q
  // Probe on P
  not not_1 (not_1_out, Q);
  // Probe on not_1_out
  or or_1 (R, P, not_1_out);
  // Probe on R
endmodule
