// Logisim project circuito_ejemplo3b.circ as structural Verilog: 1 circuit, main circuit main
module main (
  input  P,
  input  Q,
  output R
);

  wire and_1_out, not_1_out, or_1_out;

  // Probe on P
  // Probe on Q
  or or_1 (or_1_out, P, Q);
  and and_1 (and_1_out, P, Q);
  // Probe on or_1_out
  // Probe on and_1_out
  not not_1 (not_1_out, and_1_out);
  // Probe on not_1_out
  // Probe on R
  and and_2 (R, or_1_out, not_1_out);
endmodule
