// Logisim project circuito_ejemplo4b.circ as structural Verilog: 1 circuit, main circuit main
module main (
  input  P,
  input  Q,
  output R
);

  wire and_1_out, not_1_out, not_2_out;

  not not_1 (not_1_out, P);
  and and_1 (and_1_out, not_1_out, Q);
  not not_2 (not_2_out, Q);
  or or_1 (R, and_1_out, not_2_out);
endmodule
