// Logisim project circuito1a.circ as structural Verilog: 1 circuit, main circuit main
module main (
  input  A,
  input  B,
  input  C,
  input  D,
  output X
);

  wire and_1_out, and_2_out, not_1_out, not_2_out, not_3_out, not_4_out;

  // Probe on not_1_out
  not not_1 (not_1_out, A);
  not not_2 (not_2_out, B);
  not not_3 (not_3_out, C);
  // Probe on not_2_out
  // Probe on not_3_out
  // Probe on and_1_out
  and and_1 (and_1_out, not_1_out, not_2_out, not_3_out);
  not not_4 (not_4_out, and_1_out);
  and and_2 (and_2_out, not_4_out, C);
  // Probe on not_4_out
  // Probe on D
  // Probe on and_2_out
  or or_1 (X, and_2_out, not_4_out, D);
endmodule
