// Logisim project circuito1b.circ as structural Verilog: 1 circuit, main circuit main
module main (
  input  A,
  input  B,
  input  C,
  input  D,
  output X
);

  or or_1 (X, A, B, C, D);
endmodule
