// Logisim project ejemplo1_f_no_simplificada.circ as structural Verilog: 1 circuit, main circuit main
module main (
  input  a,
  input  b,
  output f
);

  wire and_1_out, and_2_out, and_3_out, not_1_out, not_2_out;

  not not_1 (not_1_out, a);
  not not_2 (not_2_out, b);
  and and_1 (and_1_out, a, b);
  and and_2 (and_2_out, a, not_2_out);
  and and_3 (and_3_out, not_1_out, b);
  or or_1 (f, and_1_out, and_2_out, and_3_out);

  // Notes on the sheet:
  //   a'
  //   b'
  //   ab
  //   ab'
  //   a'b
endmodule
