// Logisim project ejemplo2_f1_canonica.circ as structural Verilog: 2 circuits, main circuit main
module main (
  input  M,
  input  P,
  input  N,
  input  L,
  output A
);

  alama alama_1 (.M(M), .P(P), .N(N), .L(L), .A(A));
endmodule

module alama (
  input  M,
  input  P,
  input  N,
  input  L,
  output A
);

  wire and_1_out, and_2_out, and_3_out, and_4_out, and_5_out, not_1_out, not_2_out, not_3_out;

  not not_1 (not_1_out, P);
  not not_2 (not_2_out, N);
  not not_3 (not_3_out, L);
  and and_1 (and_1_out, M, not_1_out, N, not_3_out);
  and and_2 (and_2_out, M, P, not_2_out, not_3_out);
  and and_3 (and_3_out, M, P, not_2_out, L);
  and and_4 (and_4_out, M, P, N, not_3_out);
  and and_5 (and_5_out, M, P, N, L);
  or or_1 (A, and_1_out, and_2_out, and_3_out, and_4_out, and_5_out);

  // Notes on the sheet:
  //   P'
  //   N'
  //   L'
  //   MP'NL'
  //   MPN'L'
  //   MPN'L
  //   MPNL'
  //   MPNL
endmodule
