// Logisim project ejemplo2_f1_no_simplificada.circ as structural Verilog: 2 circuits, main circuit main
module main (
  input  M,
  input  P,
  input  N,
  input  L,
  output A
);

  alama alama_1 (.M(M), .P(P), .N(N), .L(L), .A(A));
endmodule

module alama (
  input  M,
  input  P,
  input  N,
  input  L,
  output A
);

  wire and_1_out, and_2_out, not_1_out;

  not not_1 (not_1_out, L);
  and and_1 (and_1_out, M, P);
  and and_2 (and_2_out, M, N, not_1_out);
  or or_1 (A, and_1_out, and_2_out);

  // Notes on the sheet:
  //   L'
  //   MP
  //   MNL'
  //   MP+MNL'
endmodule
