// Logisim project ejemplo2_f1_simplificada.circ as structural Verilog: 2 circuits, main circuit main
module main (
  input  M,
  input  P,
  input  N,
  input  L,
  output A
);

  alarma1 alarma1_1 (.M(M), .P(P), .N(N), .L(L), .A(A));
endmodule

module alarma1 (
  input  M,
  input  P,
  input  N,
  input  L,
  output A
);

  wire and_1_out, not_1_out, or_1_out;

  not not_1 (not_1_out, L);
  and and_1 (and_1_out, N, not_1_out);
  or or_1 (or_1_out, P, and_1_out);
  and and_2 (A, M, or_1_out);

  // Notes on the sheet:
  //   L'
  //   NL'
  //   P+NL'
  //   M(P+NL')
endmodule
