// Logisim project circuito2.circ as structural Verilog: 1 circuit, main circuit main
module main (
  input  T,
  input  P,
  output A
);

  wire not_1_out, not_2_out;

  not not_1 (not_1_out, T);
  not not_2 (not_2_out, P);
  and and_1 (A, not_1_out, not_2_out);
endmodule
