// Logisim project circuito_ejemplo1a.circ as structural Verilog: 1 circuit, main circuit main
module main (
  input  P,
  input  Q,
  output R
);

  wire not_1_out;

  // Probe on P
  // Probe on Q
  // Probe on not_1_out
  not not_1 (not_1_out, P);
  and and_1 (R, not_1_out, Q);
  // Probe on R
endmodule
