// Logisim project circuito_ejemplo1b.circ as structural Verilog: 1 circuit, main circuit main
module main (
  input  P,
  input  Q,
  input  R,
  output S
);

  wire not_1_out, or_1_out;

  // Probe on P
  // Probe on or_1_out
  or or_1 (or_1_out, P, Q);
  // Probe on R
  // Probe on not_1_out
  not not_1 (not_1_out, or_1_out);
  // Probe on S
  and and_1 (S, not_1_out, R);
endmodule
