// Logisim project circuito_ejemplo5.circ as structural Verilog: 1 circuit, main circuit main
module main (
  input  P,
  input  Q,
  input  R,
  output S
);

  wire and_1_out, and_2_out, and_3_out, not_1_out, not_2_out, not_3_out;

  not not_1 (not_1_out, Q);
  not not_2 (not_2_out, Q);
  not not_3 (not_3_out, R);
  and and_1 (and_1_out, P, Q, R);
  and and_2 (and_2_out, P, not_1_out, R);
  and and_3 (and_3_out, P, not_2_out, not_3_out);
  or or_1 (S, and_1_out, and_2_out, and_3_out);
endmodule
