// Logisim project alarmaTanques.circ as structural Verilog: 2 circuits, main circuit main
module main (
  input  A,
  input  B,
  input  C,
  output S
);

  alarma alarma_1 (.A(A), .B(B), .C(C), .S(S));
endmodule

module alarma (
  input  A,
  input  B,
  input  C,
  output S
);

  wire and_1_out, and_2_out, xor_1_out;

  xor xor_1 (xor_1_out, B, C);
  and and_1 (and_1_out, B, C);
  and and_2 (and_2_out, A, xor_1_out);
  or or_1 (S, and_2_out, and_1_out);
endmodule
