// Logisim project ejemplo2_clase.circ as structural Verilog: 2 circuits, main circuit main
module main (
  input  R,
  input  S,
  input  T,
  output Q
);

  circuito2 circuito2_1 (.R(R), .S(S), .T(T), .Q(Q));
endmodule

module circuito2 (
  input  R,
  input  S,
  input  T,
  output Q
);

  wire and_1_out, not_1_out, not_2_out, or_1_out;

  and and_1 (and_1_out, R, S, T);
  or or_1 (or_1_out, R, S, T);
  not not_1 (not_1_out, and_1_out);
  not not_2 (not_2_out, or_1_out);
  and and_2 (Q, not_1_out, not_2_out);
endmodule
