// Logisim project circuito1_simplificado.circ as structural Verilog: 1 circuit, main circuit main
module main (
  input  x,
  input  y,
  input  z,
  output f
);

  wire not_1_out, not_2_out, not_3_out, or_1_out, or_2_out, or_3_out;

  not not_1 (not_1_out, y);
  or or_1 (or_1_out, x, not_1_out);
  or or_2 (or_2_out, x, z);
  not not_2 (not_2_out, or_1_out);
  or or_3 (or_3_out, not_2_out, or_2_out);
  not not_3 (not_3_out, or_3_out);
  or or_4 (f, not_3_out, y);
endmodule
